# Fritzing sketch ESP32 LORA TX RX 1LED 1push button (saved by Fritzing 0.9.3b)

parts:
  esp1 = ESP32 DevKitc V4
  M1 = Osoyoo SX1278-ra-02
  R1 = Resistor [tolerance=±10% resistance=330 package=THT]
  LED1 = LED - 5mm [color="Red (633nm)" package="5 mm [THT]"]
  S1 = Pushbutton [package="[THT]"]
  R2 = Resistor [tolerance=±5% resistance=10k package=THT]

nets:
  N1: esp1.IO2, M1.DIO0
  N2: esp1.IO5, M1.NSS
  N3: esp1.IO18, M1.SCK
  N4: esp1.IO19, M1.MISO
  N5: esp1.IO23, M1.MOSI
  N6: esp1.GND#18, M1.GND
  3V3: esp1.3V3, M1.3.3V, R2.Pin_0
  N7: esp1.IO35, S1.Pin_3, S1.Pin_4, R2.Pin_1
  N8: esp1.IO14, M1.RST
  N9: R1.Pin_0, LED1.anode

custom parts:
  ESP32 DevKitc V4: ESP32-DevKitC board with ESP32-WROOM-32 module. ESP32-DevKitC V4 is a small-sized ESP32-based development board produced by Espressif. Most of the pins on the ESP module are broken out to the pin headers on the board. The pins D0, D1, D2, D3, CMD and CLK are used internally for communication between ESP32 and SPI flash memory. They are grouped on both sides near the USB connector. Avoid using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
  Osoyoo SX1278-ra-02: Osoyoo Long Distance wireless transceiver Uart LoRa Module.
